# Fritzing sketch wiring_LolinD32 (saved by Fritzing 1.0.2b)
perfboards: 1

parts:
  IC1 = ULN2003A [package="DIP16 [THT]"]
  R3 = Resistor [tolerance=±5% resistance=1.2 power=0.25W package=THT]  # not connected
  R4 = Resistor [tolerance=±5% resistance=1M power=0.25W package=THT]
  R5 = Resistor [tolerance=±5% resistance=147k power=0.25W package=THT]  # not connected
  J1 = screw terminal, 3 pins
  J3 = Terminal Block - 3 pins [package=THT]
  J4 = Terminal Block - 2 pins [package=THT]
  R6 = Resistor [tolerance=±5% resistance=10k power=0.25W package=THT]
  J6 = Terminal Block - 2 pins [package=THT]
  R7 = Resistor [tolerance=±5% resistance=330 power=0.25W package=THT]
  R1 = Resistor [tolerance=±5% resistance=1k power=0.25W package=THT]
  R2 = Resistor [tolerance=±5% resistance=1.2 power=0.25W package=THT]
  U1 = TSR12450
  U2 = Wemos Lolin D32

nets:
  N1: IC1.In_1, R1.Pin_0
  N2: IC1.0V, U2.pin_18, U2.pin_33
  N3: IC1.Out_1, R2.Pin_0
  N4: R4.Pin_1, U2.pin_9
  N5: J1.pin1, J3.Line_3, R2.Pin_1
  N6: J1.pin3, J3.Line_2, U1.GND
  N7: J3.Line_1, U1.IN
  N8: J4.Line_1, R6.Pin_0
  N9: J4.Line_2, U2.pin_0
  N10: J6.Line_1, R7.Pin_0
  N11: J6.Line_2, U2.pin_11
  N12: R1.Pin_1, U2.pin_10
  N13: U1.OUT, U2.pin_13

notes:
  A (24V Bus)
  B (GND Bus)
  P (24V)

custom parts:
  Terminal Block - 3 pins: Generic Screw Terminal 9.5mm
  Terminal Block - 2 pins: Generic Screw Terminal 9.5mm
  TSR12450: Mini DC/DC Step-Down (Buck) Converter - 5V @ 1A output - TSR12450
  Wemos Lolin D32: Wemos Lolin D32 wifi and blue tooth board based on the ESP-32 cpu, digital I/Os 22, analog inputs 6, analog outputs 2 clock 240mhz, Flash 4Mbytes, lipo battery charger (500ma connection broken out on breadboard but not pcb), usb. The mounting holes are only set on the silkscreen, if you want actual holes in the pcb copy the hole from the pcb menu in parts over the top of the hole in the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
